// Logisim project LogicProject.circ as structural Verilog: 21 circuits, main circuit main
module main (
  input  Clear
);

  wire CF, Clock_out, CMP_Signal, Fetch_Instruction, Instr_Read, IR_6, Jump_Signal, MemRead, MemWrite,
       PC_Read, PC_Write, Read_Enable_1, Read_Enable_2, Write_Enable, ZF;
  wire [1:0] IR_16_15;
  wire [2:0] IR_13_11;
  wire [3:0] Read_Reg_1, Read_Reg_2, Write_Reg;
  wire [5:0] IMM;
  wire [10:0] ADDRESS, controlled_buffer_1_out, Jump_Address, multiplexer_1_out, n11_bit_adder_1_output,
       PC_Address;
  wire [17:0] INSTRUCTION, Read_Data_1, Read_Data_2, Write_Data;

  Clock Clock (.out(Clock_out));
  _11_bit_Adder u_11_bit_adder_1 (.SRC2(11'h1), .Output(n11_bit_adder_1_output), .SRC1(PC_Address), .CarryIn(1'b0));
  Multiplexer #(.width(11), .enable("false")) multiplexer_1 (
    .in0(n11_bit_adder_1_output), .in1(Jump_Address), .out(multiplexer_1_out), .sel(Jump_Signal));
  Comparator comparator_1 (
    .CMP1(Read_Data_1), .CMP2(Read_Data_2), .CMP_signal(CMP_Signal), .Clock(Clock_out), .ZF(ZF), .CF(CF),
    .Clear(Clear));
  Program_Counter program_counter_1 (
    .\input (multiplexer_1_out), .Enable(PC_Read), .Clock(Clock_out), .\output (PC_Address),
    .write(PC_Write), .Clear(Clear));
  Control_Unit control_unit_1 (
    .Instruction(INSTRUCTION), .CMP_Signal(CMP_Signal), .ADDRESS(ADDRESS), .IMM(IMM), .IR_6(IR_6),
    .IR_16_15(IR_16_15), .Write_Enable(Write_Enable), .Read_Enable_1(Read_Enable_1),
    .Read_Enable_2(Read_Enable_2), .Write_Reg(Write_Reg), .MemWrite(MemWrite), .MemRead(MemRead),
    .Jump_Signal(Jump_Signal), .IR_13_11(IR_13_11), .Read_Reg_1(Read_Reg_1), .InstrRead(Instr_Read),
    .PCread(PC_Read), .PCwrite(PC_Write), .Read_Reg_2(Read_Reg_2), .Clear_FSM(Clear), .Clock(Clock_out),
    .Fetch_Instruction(Fetch_Instruction));
  assign controlled_buffer_1_out = Fetch_Instruction ? PC_Address : 11'bz;  // Controlled_Buffer controlled_buffer_1
  ROM #(.addrWidth(11), .dataWidth(18)) rom_1 (.addr(controlled_buffer_1_out), .data(INSTRUCTION), .sel(1'b1));
  Jump jump_1 (
    .ZF(ZF), .CF(CF), .Jump_Signal(Jump_Signal), .IR_13_11(IR_13_11), .Jump_Address(Jump_Address),
    .PC(PC_Address), .ADDRESS(ADDRESS));
  RegisterFile registerfile_1 (
    .ReadData_1(Read_Data_1), .WriteData(Write_Data), .Clock(Clock_out), .Clear(Clear), .WriteReg(Write_Reg),
    .Read_Enable_1(Read_Enable_1), .ReadReg1(Read_Reg_1), .Write_Enable(Write_Enable),
    .Read_Enable_2(Read_Enable_2), .ReadReg2(Read_Reg_2), .ReadData_2(Read_Data_2));
  ALU alu_1 (.SRC1(Read_Data_1), .SRC2(Read_Data_2), .IMM(IMM), .IR_16_15(IR_16_15), .Output(Write_Data), .IR_6(IR_6));
  RAM #(.addrWidth(11), .dataWidth(18), .bus("separate")) ram_1 (
    .addr(ADDRESS), .din(Read_Data_1), .data(Write_Data), .str(MemWrite), .sel(1'b1), .clk(Clock_out),
    .ld(MemRead), .clr(1'b0));

  // Notes on the sheet:
  //   Instruction Memory
  //   contents of rom_1 (hex, n*v repeats v):
  //   20000 20801 1001 9801 12001 1a801 3045 b843 28864 24064 30080 397f5 387f4
  //   Data Memory
endmodule

module Control_Unit (
  input  Clear_FSM,
  input  Clock,
  input  [17:0] Instruction,
  output CMP_Signal,
  output [10:0] ADDRESS,
  output [5:0] IMM,
  output IR_6,
  output [1:0] IR_16_15,
  output Write_Enable,
  output Read_Enable_1,
  output Read_Enable_2,
  output [3:0] Write_Reg,
  output MemWrite,
  output MemRead,
  output Jump_Signal,
  output [2:0] IR_13_11,
  output [3:0] Read_Reg_1,
  output Fetch_Instruction,
  output PCwrite,
  output [3:0] Read_Reg_2,
  output InstrRead,
  output PCread
);

  wire ADD, ADDI, AND, and_10_out, and_11_out, ANDI, CMP, decoder_1_out0, decoder_1_out1, decoder_1_out2,
       decoder_1_out3, decoder_1_out4, decoder_1_out9, LD, NAND, NOR, or_2_out, or_5_out, or_6_out, or_7_out,
       or_8_out, or_9_out, or_10_out, ST;
  wire [1:0] or_4_out;
  wire [1:1] or_1_out;
  wire [3:0] fsm_1_output;

  or or_1 (or_1_out[1], ADD, AND, NAND, NOR);
  or or_2 (or_2_out, ADD, ADDI, AND, ANDI, NAND, NOR, LD);
  or or_3 (or_4_out[1], ST, CMP);
  or or_4 (or_4_out[0], ADD, ADDI, AND, ANDI, NAND, NOR);
  assign Write_Reg = or_2_out ? Instruction[14:11] : 4'bz;  // Controlled_Buffer controlled_buffer_1
  or or_5 (or_5_out, or_4_out[1], or_4_out[0]);
  Multiplexer #(.select(2), .width(4)) multiplexer_1 (
    .in1(Instruction[10:7]), .in2(Instruction[14:11]), .out(Read_Reg_1), .sel(or_4_out), .en(or_5_out));  // open: in0, in3
  Multiplexer #(.select(2), .width(4)) multiplexer_2 (
    .in1(Instruction[10:7]), .in2(Instruction[3:0]), .out(Read_Reg_2), .sel({or_1_out[1], CMP}), .en(or_6_out));  // open: in0, in3
  or or_6 (or_6_out, or_1_out[1], CMP);
  and and_1 (ADD, ~Instruction[17], ~Instruction[16], ~Instruction[15], ~Instruction[6]);  // AND_Gate
  and and_2 (ADDI, ~Instruction[17], ~Instruction[16], ~Instruction[15], Instruction[6]);  // AND_Gate
  and and_3 (AND, ~Instruction[17], ~Instruction[16], Instruction[15], ~Instruction[6]);  // AND_Gate
  and and_4 (ANDI, ~Instruction[17], ~Instruction[16], Instruction[15], Instruction[6]);  // AND_Gate
  and and_5 (NAND, ~Instruction[17], Instruction[16], ~Instruction[15]);  // AND_Gate
  and and_6 (NOR, ~Instruction[17], Instruction[16], Instruction[15]);  // AND_Gate
  and and_7 (LD, Instruction[17], ~Instruction[16], ~Instruction[15]);  // AND_Gate
  and and_8 (ST, Instruction[17], ~Instruction[16], Instruction[15]);  // AND_Gate
  and and_9 (CMP, Instruction[17], Instruction[16], ~Instruction[15]);  // AND_Gate
  FSM fsm_1 (.OPCODE(Instruction[17:15]), .Output(fsm_1_output), .Clock(Clock), .Clear(Clear_FSM));
  // Probe on fsm_1_output
  Decoder #(.select(4), .enable("false")) decoder_1 (
    .out0(decoder_1_out0), .out1(decoder_1_out1), .out2(decoder_1_out2), .out3(decoder_1_out3),
    .out4(decoder_1_out4), .out5(MemWrite), .out6(CMP_Signal), .out7(Jump_Signal), .out8(Fetch_Instruction),
    .out9(decoder_1_out9), .sel(fsm_1_output));  // open: out10, out11, out12, out13, out14, out15
  or or_7 (or_7_out, decoder_1_out0, decoder_1_out1);
  and and_10 (and_10_out, decoder_1_out0, ~Instruction[6]);  // AND_Gate
  and and_11 (and_11_out, decoder_1_out1, ~Instruction[6]);  // AND_Gate
  or or_8 (or_8_out, decoder_1_out4, MemWrite, Jump_Signal, decoder_1_out9);
  or or_9 (or_9_out, decoder_1_out0, decoder_1_out1);
  and and_12 (IR_6, Instruction[6], or_7_out);
  or or_10 (or_10_out, decoder_1_out0, decoder_1_out1, decoder_1_out2, decoder_1_out3);
  assign ADDRESS = or_8_out ? Instruction[10:0] : 11'bz;  // Controlled_Buffer controlled_buffer_2
  assign IMM = or_9_out ? Instruction[5:0] : 6'bz;  // Controlled_Buffer controlled_buffer_3
  assign IR_16_15 = or_10_out ? Instruction[16:15] : 2'bz;  // Controlled_Buffer controlled_buffer_4
  or or_11 (Write_Enable, decoder_1_out0, decoder_1_out1, decoder_1_out2, decoder_1_out3, decoder_1_out9);
  or or_12 (Read_Enable_1, decoder_1_out0, decoder_1_out1, decoder_1_out2, decoder_1_out3, MemWrite, CMP_Signal);
  or or_13 (Read_Enable_2, and_10_out, and_11_out, decoder_1_out2, decoder_1_out3, CMP_Signal);
  or or_14 (MemRead, decoder_1_out4, decoder_1_out9);
  assign IR_13_11 = Jump_Signal ? Instruction[13:11] : 3'bz;  // Controlled_Buffer controlled_buffer_5
  or or_15 (PCwrite, decoder_1_out0, decoder_1_out1, decoder_1_out2, decoder_1_out3, MemWrite, CMP_Signal, Jump_Signal, decoder_1_out9);

  assign InstrRead = 1'b1;
  assign PCread = 1'b1;

  // Other names for the same wires on the sheet: Reg_2[3:0] = Instruction[10:7]; Reg_3[3:0] = Instruction[3:0];
  //   Reg_1[3:0] = Instruction[14:11]

  // Notes on the sheet:
  //   ADD/I
  //   AND/I
  //   NAND
  //   NOR
  //   LD 1
  //   ST
  //   CMP
  //   JUMP
  //   Fetch
  //   LD 2
endmodule

// Register File
module RegisterFile (
  input  [17:0] WriteData,
  input  Clock,
  input  Clear,
  input  [3:0] WriteReg,
  input  Read_Enable_1,
  input  [3:0] ReadReg1,
  input  Write_Enable,
  input  Read_Enable_2,
  input  [3:0] ReadReg2,
  output [17:0] ReadData_1,
  output [17:0] ReadData_2
);

  wire and_1_out, and_2_out, and_3_out, and_4_out, and_5_out, and_6_out, and_7_out, and_8_out, and_9_out,
       and_10_out, and_11_out, and_12_out, and_13_out, and_14_out, and_15_out, and_16_out, and_17_out,
       and_18_out, and_19_out, and_20_out, and_21_out, and_22_out, and_23_out, and_24_out, and_25_out,
       and_26_out, and_27_out, and_28_out, and_29_out, and_30_out, and_31_out, and_32_out, and_33_out,
       and_34_out, and_35_out, and_36_out, and_37_out, and_38_out, and_39_out, and_40_out, and_41_out,
       and_42_out, and_43_out, and_44_out, and_45_out, and_46_out, and_47_out, and_48_out, decoder_1_out0,
       decoder_1_out1, decoder_1_out2, decoder_1_out3, decoder_1_out4, decoder_1_out5, decoder_1_out6,
       decoder_1_out7, decoder_1_out8, decoder_1_out9, decoder_1_out10, decoder_1_out11, decoder_1_out12,
       decoder_1_out13, decoder_1_out14, decoder_1_out15, decoder_2_out0, decoder_2_out1, decoder_2_out2,
       decoder_2_out3, decoder_2_out4, decoder_2_out5, decoder_2_out6, decoder_2_out7, decoder_2_out8,
       decoder_2_out9, decoder_2_out10, decoder_2_out11, decoder_2_out12, decoder_2_out13, decoder_2_out14,
       decoder_2_out15, decoder_3_out0, decoder_3_out1, decoder_3_out2, decoder_3_out3, decoder_3_out4,
       decoder_3_out5, decoder_3_out6, decoder_3_out7, decoder_3_out8, decoder_3_out9, decoder_3_out10,
       decoder_3_out11, decoder_3_out12, decoder_3_out13, decoder_3_out14, decoder_3_out15;
  wire [17:0] register_1_q, register_2_q, register_3_q, register_4_q, register_5_q, register_6_q,
       register_7_q, register_8_q, register_9_q, register_10_q, register_11_q, register_12_q, register_13_q,
       register_14_q, register_15_q, register_16_q;

  Decoder #(.select(4), .enable("false")) decoder_1 (
    .out0(decoder_1_out0), .out1(decoder_1_out1), .out2(decoder_1_out2), .out3(decoder_1_out3),
    .out4(decoder_1_out4), .out5(decoder_1_out5), .out6(decoder_1_out6), .out7(decoder_1_out7),
    .out8(decoder_1_out8), .out9(decoder_1_out9), .out10(decoder_1_out10), .out11(decoder_1_out11),
    .out12(decoder_1_out12), .out13(decoder_1_out13), .out14(decoder_1_out14), .out15(decoder_1_out15),
    .sel(WriteReg));
  and and_1 (and_1_out, Write_Enable, decoder_1_out14);
  and and_2 (and_2_out, Write_Enable, decoder_1_out15);
  and and_3 (and_3_out, Write_Enable, decoder_1_out12);
  and and_4 (and_4_out, Write_Enable, decoder_1_out13);
  and and_5 (and_5_out, Write_Enable, decoder_1_out11);
  and and_6 (and_6_out, Write_Enable, decoder_1_out10);
  and and_7 (and_7_out, Write_Enable, decoder_1_out9);
  and and_8 (and_8_out, Write_Enable, decoder_1_out6);
  and and_9 (and_9_out, Write_Enable, decoder_1_out8);
  and and_10 (and_10_out, Write_Enable, decoder_1_out7);
  and and_11 (and_11_out, Write_Enable, decoder_1_out5);
  and and_12 (and_12_out, Write_Enable, decoder_1_out4);
  and and_13 (and_13_out, Write_Enable, decoder_1_out3);
  and and_14 (and_14_out, Write_Enable, decoder_1_out2);
  and and_15 (and_15_out, Write_Enable, decoder_1_out1);
  and and_16 (and_16_out, Write_Enable, decoder_1_out0);
  Register #(.width(18)) register_1 (.D(WriteData), .en(and_16_out), .Q(register_1_q), .clk(Clock), .clr(Clear));
  Register #(.width(18)) register_2 (.D(WriteData), .en(and_15_out), .Q(register_2_q), .clk(Clock), .clr(Clear));
  Register #(.width(18)) register_3 (.D(WriteData), .en(and_14_out), .Q(register_3_q), .clk(Clock), .clr(Clear));
  Register #(.width(18)) register_4 (.D(WriteData), .en(and_13_out), .Q(register_4_q), .clk(Clock), .clr(Clear));
  Register #(.width(18)) register_5 (.D(WriteData), .en(and_12_out), .Q(register_5_q), .clk(Clock), .clr(Clear));
  Register #(.width(18)) register_6 (.D(WriteData), .en(and_11_out), .Q(register_6_q), .clk(Clock), .clr(Clear));
  Register #(.width(18)) register_7 (.D(WriteData), .en(and_8_out), .Q(register_7_q), .clk(Clock), .clr(Clear));
  Register #(.width(18)) register_8 (.D(WriteData), .en(and_10_out), .Q(register_8_q), .clk(Clock), .clr(Clear));
  Register #(.width(18)) register_9 (.D(WriteData), .en(and_9_out), .Q(register_9_q), .clk(Clock), .clr(Clear));
  Register #(.width(18)) register_10 (.D(WriteData), .en(and_7_out), .Q(register_10_q), .clk(Clock), .clr(Clear));
  Register #(.width(18)) register_11 (.D(WriteData), .en(and_6_out), .Q(register_11_q), .clk(Clock), .clr(Clear));
  Register #(.width(18)) register_12 (.D(WriteData), .en(and_5_out), .Q(register_12_q), .clk(Clock), .clr(Clear));
  Register #(.width(18)) register_13 (.D(WriteData), .en(and_3_out), .Q(register_13_q), .clk(Clock), .clr(Clear));
  Register #(.width(18)) register_14 (.D(WriteData), .en(and_4_out), .Q(register_14_q), .clk(Clock), .clr(Clear));
  Register #(.width(18)) register_15 (.D(WriteData), .en(and_1_out), .Q(register_15_q), .clk(Clock), .clr(Clear));
  Register #(.width(18)) register_16 (.D(WriteData), .en(and_2_out), .Q(register_16_q), .clk(Clock), .clr(Clear));
  // Probe on register_1_q
  // Probe on register_2_q
  // Probe on register_3_q
  // Probe on register_4_q
  // Probe on register_5_q
  // Probe on register_6_q
  // Probe on register_7_q
  // Probe on register_8_q
  // Probe on register_9_q
  // Probe on register_10_q
  // Probe on register_11_q
  // Probe on register_12_q
  // Probe on register_13_q
  // Probe on register_14_q
  // Probe on register_15_q
  // Probe on register_16_q
  assign ReadData_1 = and_35_out ? register_1_q : 18'bz;  // Controlled_Buffer controlled_buffer_1
  assign ReadData_2 = and_32_out ? register_1_q : 18'bz;  // Controlled_Buffer controlled_buffer_2
  assign ReadData_1 = and_34_out ? register_2_q : 18'bz;  // Controlled_Buffer controlled_buffer_3
  assign ReadData_2 = and_30_out ? register_2_q : 18'bz;  // Controlled_Buffer controlled_buffer_4
  assign ReadData_1 = and_33_out ? register_3_q : 18'bz;  // Controlled_Buffer controlled_buffer_5
  assign ReadData_2 = and_31_out ? register_3_q : 18'bz;  // Controlled_Buffer controlled_buffer_6
  assign ReadData_1 = and_37_out ? register_4_q : 18'bz;  // Controlled_Buffer controlled_buffer_7
  assign ReadData_2 = and_28_out ? register_4_q : 18'bz;  // Controlled_Buffer controlled_buffer_8
  assign ReadData_1 = and_36_out ? register_5_q : 18'bz;  // Controlled_Buffer controlled_buffer_9
  assign ReadData_2 = and_29_out ? register_5_q : 18'bz;  // Controlled_Buffer controlled_buffer_10
  assign ReadData_1 = and_40_out ? register_6_q : 18'bz;  // Controlled_Buffer controlled_buffer_11
  assign ReadData_2 = and_26_out ? register_6_q : 18'bz;  // Controlled_Buffer controlled_buffer_12
  assign ReadData_1 = and_39_out ? register_7_q : 18'bz;  // Controlled_Buffer controlled_buffer_13
  assign ReadData_2 = and_27_out ? register_7_q : 18'bz;  // Controlled_Buffer controlled_buffer_14
  assign ReadData_1 = and_38_out ? register_8_q : 18'bz;  // Controlled_Buffer controlled_buffer_15
  assign ReadData_2 = and_25_out ? register_8_q : 18'bz;  // Controlled_Buffer controlled_buffer_16
  assign ReadData_1 = and_43_out ? register_9_q : 18'bz;  // Controlled_Buffer controlled_buffer_17
  assign ReadData_2 = and_24_out ? register_9_q : 18'bz;  // Controlled_Buffer controlled_buffer_18
  assign ReadData_1 = and_42_out ? register_10_q : 18'bz;  // Controlled_Buffer controlled_buffer_19
  assign ReadData_2 = and_23_out ? register_10_q : 18'bz;  // Controlled_Buffer controlled_buffer_20
  assign ReadData_1 = and_41_out ? register_11_q : 18'bz;  // Controlled_Buffer controlled_buffer_21
  assign ReadData_2 = and_22_out ? register_11_q : 18'bz;  // Controlled_Buffer controlled_buffer_22
  assign ReadData_1 = and_45_out ? register_12_q : 18'bz;  // Controlled_Buffer controlled_buffer_23
  assign ReadData_2 = and_20_out ? register_12_q : 18'bz;  // Controlled_Buffer controlled_buffer_24
  assign ReadData_1 = and_44_out ? register_13_q : 18'bz;  // Controlled_Buffer controlled_buffer_25
  assign ReadData_2 = and_21_out ? register_13_q : 18'bz;  // Controlled_Buffer controlled_buffer_26
  assign ReadData_1 = and_48_out ? register_14_q : 18'bz;  // Controlled_Buffer controlled_buffer_27
  assign ReadData_2 = and_18_out ? register_14_q : 18'bz;  // Controlled_Buffer controlled_buffer_28
  assign ReadData_1 = and_47_out ? register_15_q : 18'bz;  // Controlled_Buffer controlled_buffer_29
  assign ReadData_2 = and_19_out ? register_15_q : 18'bz;  // Controlled_Buffer controlled_buffer_30
  assign ReadData_1 = and_46_out ? register_16_q : 18'bz;  // Controlled_Buffer controlled_buffer_31
  assign ReadData_2 = and_17_out ? register_16_q : 18'bz;  // Controlled_Buffer controlled_buffer_32
  and and_17 (and_17_out, decoder_2_out15, Read_Enable_2);
  and and_18 (and_18_out, decoder_2_out13, Read_Enable_2);
  and and_19 (and_19_out, decoder_2_out14, Read_Enable_2);
  and and_20 (and_20_out, decoder_2_out11, Read_Enable_2);
  and and_21 (and_21_out, decoder_2_out12, Read_Enable_2);
  and and_22 (and_22_out, decoder_2_out10, Read_Enable_2);
  and and_23 (and_23_out, decoder_2_out9, Read_Enable_2);
  and and_24 (and_24_out, decoder_2_out8, Read_Enable_2);
  and and_25 (and_25_out, decoder_2_out7, Read_Enable_2);
  and and_26 (and_26_out, decoder_2_out5, Read_Enable_2);
  and and_27 (and_27_out, decoder_2_out6, Read_Enable_2);
  and and_28 (and_28_out, decoder_2_out3, Read_Enable_2);
  and and_29 (and_29_out, decoder_2_out4, Read_Enable_2);
  and and_30 (and_30_out, decoder_2_out1, Read_Enable_2);
  and and_31 (and_31_out, decoder_2_out2, Read_Enable_2);
  and and_32 (and_32_out, decoder_2_out0, Read_Enable_2);
  and and_33 (and_33_out, Read_Enable_1, decoder_3_out2);
  and and_34 (and_34_out, Read_Enable_1, decoder_3_out1);
  and and_35 (and_35_out, Read_Enable_1, decoder_3_out0);
  and and_36 (and_36_out, Read_Enable_1, decoder_3_out4);
  and and_37 (and_37_out, Read_Enable_1, decoder_3_out3);
  and and_38 (and_38_out, Read_Enable_1, decoder_3_out7);
  and and_39 (and_39_out, Read_Enable_1, decoder_3_out6);
  and and_40 (and_40_out, Read_Enable_1, decoder_3_out5);
  and and_41 (and_41_out, Read_Enable_1, decoder_3_out10);
  and and_42 (and_42_out, Read_Enable_1, decoder_3_out9);
  and and_43 (and_43_out, Read_Enable_1, decoder_3_out8);
  and and_44 (and_44_out, Read_Enable_1, decoder_3_out12);
  and and_45 (and_45_out, Read_Enable_1, decoder_3_out11);
  and and_46 (and_46_out, Read_Enable_1, decoder_3_out15);
  and and_47 (and_47_out, Read_Enable_1, decoder_3_out14);
  and and_48 (and_48_out, Read_Enable_1, decoder_3_out13);
  Decoder #(.select(4), .enable("false")) decoder_2 (
    .out0(decoder_2_out0), .out1(decoder_2_out1), .out2(decoder_2_out2), .out3(decoder_2_out3),
    .out4(decoder_2_out4), .out5(decoder_2_out5), .out6(decoder_2_out6), .out7(decoder_2_out7),
    .out8(decoder_2_out8), .out9(decoder_2_out9), .out10(decoder_2_out10), .out11(decoder_2_out11),
    .out12(decoder_2_out12), .out13(decoder_2_out13), .out14(decoder_2_out14), .out15(decoder_2_out15),
    .sel(ReadReg2));
  // Probe on ReadData_2
  // Probe on ReadData_1
  Decoder #(.select(4), .enable("false")) decoder_3 (
    .out0(decoder_3_out0), .out1(decoder_3_out1), .out2(decoder_3_out2), .out3(decoder_3_out3),
    .out4(decoder_3_out4), .out5(decoder_3_out5), .out6(decoder_3_out6), .out7(decoder_3_out7),
    .out8(decoder_3_out8), .out9(decoder_3_out9), .out10(decoder_3_out10), .out11(decoder_3_out11),
    .out12(decoder_3_out12), .out13(decoder_3_out13), .out14(decoder_3_out14), .out15(decoder_3_out15),
    .sel(ReadReg1));

  // Notes on the sheet:
  //   Write Decoder
  //   Read Decoder2
  //   Read Decoder1
endmodule

module FSM (
  input  [2:0] OPCODE,
  input  Clock,
  input  Clear,
  output [3:0] Output
);

  wire [1:0] and_2_out;
  wire [3:0] register_1_q;

  Register #(.width(4)) register_1 (.D(Output), .en(1'b1), .Q(register_1_q), .clk(Clock), .clr(Clear));
  // Probe on register_1_q
  and and_1 (and_2_out[1], register_1_q[3], ~register_1_q[2], ~register_1_q[1], ~register_1_q[0]);  // AND_Gate
  and and_2 (and_2_out[0], ~register_1_q[3], register_1_q[2], ~register_1_q[1], ~register_1_q[0]);  // AND_Gate
  Multiplexer #(.select(2), .width(4), .enable("false")) multiplexer_1 (
    .in0(4'b1000), .in1(4'b1001), .in2({1'b0, OPCODE}), .out(Output), .sel(and_2_out));  // open: in3
endmodule

// ALIU
module ALU (
  input  [17:0] SRC1,
  input  [17:0] SRC2,
  input  [5:0] IMM,
  input  IR_6,
  input  [1:0] IR_16_15,
  output [17:0] Output
);

  wire [17:0] and_1_out, multiplexer_1_out, n18_bit_adder_1_output, nand_1_out, nor_1_out,
       sign_extender_1__18_bit_output;

  Sign_Extender sign_extender_1 (._6_bit_input(IMM), ._18_bit_output(sign_extender_1__18_bit_output));
  Multiplexer #(.width(18), .enable("false")) multiplexer_1 (
    .in0(SRC2), .in1(sign_extender_1__18_bit_output), .out(multiplexer_1_out), .sel(IR_6));
  _18_bit_adder u_18_bit_adder_1 (
    .SRC2(multiplexer_1_out), .Output(n18_bit_adder_1_output), .SRC1(SRC1), .CarryIn(1'b0));
  assign and_1_out = SRC1 & multiplexer_1_out;  // AND_Gate and_1, 18 bits wide
  assign nand_1_out = ~(SRC1 & SRC2);  // NAND_Gate nand_1, 18 bits wide
  assign nor_1_out = ~(SRC1 | SRC2);  // NOR_Gate nor_1, 18 bits wide
  Multiplexer #(.select(2), .width(18), .enable("false")) multiplexer_2 (
    .in0(n18_bit_adder_1_output), .in1(and_1_out), .in2(nand_1_out), .in3(nor_1_out), .out(Output),
    .sel(IR_16_15));
endmodule

module Comparator (
  input  [17:0] CMP1,
  input  [17:0] CMP2,
  input  CMP_signal,
  input  Clock,
  input  Clear,
  output ZF,
  output CF
);

  wire and_1_out, and_2_out, Comparator_a_b, Comparator_a_b_2, Comparator_a_b_3, multiplexer_1_out,
       multiplexer_2_out, multiplexer_3_out, multiplexer_4_out;

  _18_bit_Comparator Comparator (
    .A(CMP1), .B(CMP2), .A_B(Comparator_a_b), .A_B_2(Comparator_a_b_2), .A_B_3(Comparator_a_b_3));
  and and_1 (and_1_out, ~Comparator_a_b, ~Comparator_a_b_2, Comparator_a_b_3);  // AND_Gate
  and and_2 (and_2_out, ~Comparator_a_b, Comparator_a_b_2, ~Comparator_a_b_3);  // AND_Gate
  Multiplexer #(.enable("false")) multiplexer_1 (.in0(1'b0), .in1(1'b1), .out(multiplexer_1_out), .sel(and_1_out));
  Multiplexer #(.enable("false")) multiplexer_2 (.in0(1'b0), .in1(1'b1), .out(multiplexer_2_out), .sel(and_2_out));
  Multiplexer #(.enable("false")) multiplexer_3 (
    .in0(ZF), .in1(multiplexer_1_out), .out(multiplexer_3_out), .sel(CMP_signal));
  Multiplexer #(.enable("false")) multiplexer_4 (
    .in0(CF), .in1(multiplexer_2_out), .out(multiplexer_4_out), .sel(CMP_signal));
  Register #(.width(1)) register_1 (.D(multiplexer_3_out), .en(1'b1), .Q(ZF), .clk(Clock), .clr(Clear));
  Register #(.width(1)) register_2 (.D(multiplexer_4_out), .en(1'b1), .Q(CF), .clk(Clock), .clr(Clear));
endmodule

module Jump (
  input  Jump_Signal,
  input  [2:0] IR_13_11,
  input  [10:0] PC,
  input  [10:0] ADDRESS,
  input  ZF,
  input  CF,
  output [10:0] Jump_Address
);

  wire and_1_out, and_2_out, and_3_out, and_4_out, and_5_out, and_6_out, and_7_out, and_8_out, JA, JAE, JB,
       JBE, JE, JUMP, or_1_out, or_2_out;
  wire [10:0] multiplexer_1_out, multiplexer_2_out, multiplexer_3_out, multiplexer_4_out, multiplexer_5_out,
       n11_bit_adder_1_output, n11_bit_adder_2_output;

  and and_1 (and_1_out, ZF, ~CF);  // AND_Gate
  and and_2 (and_2_out, ~ZF, ~CF);  // AND_Gate
  and and_3 (and_3_out, ~ZF, CF);  // AND_Gate
  and and_4 (and_4_out, JE, and_1_out);
  and and_5 (and_5_out, JA, and_2_out);
  and and_6 (and_6_out, JB, and_3_out);
  and and_7 (and_7_out, JAE, or_1_out);
  or or_1 (or_1_out, and_1_out, and_2_out);
  and and_8 (and_8_out, JBE, or_2_out);
  or or_2 (or_2_out, and_3_out, and_1_out);
  Decoder #(.select(3)) decoder_1 (
    .out0(JUMP), .out1(JE), .out2(JA), .out3(JB), .out4(JAE), .out5(JBE), .sel(IR_13_11), .en(Jump_Signal));  // open: out6, out7
  _11_bit_Adder u_11_bit_adder_1 (.SRC2(PC), .Output(n11_bit_adder_1_output), .SRC1(ADDRESS), .CarryIn(1'b0));
  _11_bit_Adder u_11_bit_adder_2 (.SRC2(PC), .Output(n11_bit_adder_2_output), .SRC1(11'h1), .CarryIn(1'b0));
  Multiplexer #(.width(11), .enable("false")) multiplexer_1 (
    .in0(n11_bit_adder_2_output), .in1(n11_bit_adder_1_output), .out(multiplexer_1_out), .sel(and_4_out));
  Multiplexer #(.width(11), .enable("false")) multiplexer_2 (
    .in0(n11_bit_adder_2_output), .in1(n11_bit_adder_1_output), .out(multiplexer_2_out), .sel(and_5_out));
  Multiplexer #(.width(11), .enable("false")) multiplexer_3 (
    .in0(n11_bit_adder_2_output), .in1(n11_bit_adder_1_output), .out(multiplexer_3_out), .sel(and_6_out));
  Multiplexer #(.width(11), .enable("false")) multiplexer_4 (
    .in0(n11_bit_adder_2_output), .in1(n11_bit_adder_1_output), .out(multiplexer_4_out), .sel(and_7_out));
  Multiplexer #(.width(11), .enable("false")) multiplexer_5 (
    .in0(n11_bit_adder_2_output), .in1(n11_bit_adder_1_output), .out(multiplexer_5_out), .sel(and_8_out));
  assign Jump_Address = JUMP ? n11_bit_adder_1_output : 11'bz;  // Controlled_Buffer controlled_buffer_1
  assign Jump_Address = JE ? multiplexer_1_out : 11'bz;  // Controlled_Buffer controlled_buffer_2
  assign Jump_Address = JA ? multiplexer_2_out : 11'bz;  // Controlled_Buffer controlled_buffer_3
  assign Jump_Address = JB ? multiplexer_3_out : 11'bz;  // Controlled_Buffer controlled_buffer_4
  assign Jump_Address = JAE ? multiplexer_4_out : 11'bz;  // Controlled_Buffer controlled_buffer_5
  assign Jump_Address = JBE ? multiplexer_5_out : 11'bz;  // Controlled_Buffer controlled_buffer_6

  // Notes on the sheet:
  //   A=B
  //   A>B
  //   A<B
endmodule

// PC
module Program_Counter (
  input  write,
  input  [10:0] \input ,
  input  Enable,
  input  Clock,
  input  Clear,
  output [10:0] \output 
);

  wire [10:0] multiplexer_1_out;

  Multiplexer #(.width(11), .enable("false")) multiplexer_1 (
    .in0(\output ), .in1(\input ), .out(multiplexer_1_out), .sel(write));
  Register #(.width(11)) register_1 (.D(multiplexer_1_out), .en(Enable), .Q(\output ), .clk(Clock), .clr(Clear));
endmodule

module Sign_Extender (
  input  [5:0] _6_bit_input,
  output [17:0] _18_bit_output
);

  Multiplexer #(.width(12), .enable("false")) multiplexer_1 (
    .in0({12{1'b0}}), .in1({12{1'b1}}), .out(_18_bit_output[17:6]), .sel(_6_bit_input[5]));

  assign _18_bit_output[5:0] = _6_bit_input;
endmodule

module _2_bit_Comparator (
  input  [1:0] A,
  input  [1:0] B,
  input  in_3,
  input  in_4,
  input  in_5,
  output A_B,
  output A_B_2,
  output A_B_3
);

  wire and_1_out, and_2_out, and_3_out, and_4_out, and_5_out, nor_1_out, or_1_out, xnor_1_out, xnor_2_out;

  and and_1 (and_1_out, A[1], ~B[1]);  // AND_Gate
  and and_2 (and_2_out, ~B[0], A[0], xnor_2_out);  // AND_Gate
  xnor xnor_1 (xnor_1_out, B[0], A[0]);
  xnor xnor_2 (xnor_2_out, A[1], B[1]);
  or or_1 (or_1_out, and_1_out, and_2_out);
  and and_3 (and_3_out, xnor_1_out, xnor_2_out);
  and and_4 (and_4_out, and_3_out, in_3);
  nor nor_1 (nor_1_out, or_1_out, and_3_out);
  or or_2 (A_B, or_1_out, and_4_out);
  or or_3 (A_B_2, nor_1_out, and_5_out);
  and and_5 (and_5_out, and_3_out, in_4);
  and and_6 (A_B_3, and_3_out, in_5);
endmodule

module _4_bit_Comparator (
  input  [3:0] A,
  input  in_2,
  input  in_3,
  input  in_4,
  input  [3:0] B,
  output A_B,
  output A_B_2,
  output A_B_3
);

  wire n2_bit_comparator_2_a_b, n2_bit_comparator_2_a_b_2, n2_bit_comparator_2_a_b_3;

  _2_bit_Comparator u_2_bit_comparator_1 (
    .A(A[3:2]), .B(B[3:2]), .in_3(n2_bit_comparator_2_a_b), .in_4(n2_bit_comparator_2_a_b_2),
    .in_5(n2_bit_comparator_2_a_b_3), .A_B(A_B), .A_B_2(A_B_2), .A_B_3(A_B_3));
  _2_bit_Comparator u_2_bit_comparator_2 (
    .A(A[1:0]), .B(B[1:0]), .in_3(in_2), .in_4(in_3), .in_5(in_4), .A_B(n2_bit_comparator_2_a_b),
    .A_B_2(n2_bit_comparator_2_a_b_2), .A_B_3(n2_bit_comparator_2_a_b_3));
endmodule

module _18_bit_Comparator (
  input  [17:0] A,
  input  [17:0] B,
  output A_B,
  output A_B_2,
  output A_B_3
);

  wire n4_bit_comparator_1_a_b, n4_bit_comparator_1_a_b_2, n4_bit_comparator_1_a_b_3,
       n4_bit_comparator_2_a_b, n4_bit_comparator_2_a_b_2, n4_bit_comparator_2_a_b_3,
       n4_bit_comparator_3_a_b, n4_bit_comparator_3_a_b_2, n4_bit_comparator_3_a_b_3,
       n4_bit_comparator_4_a_b, n4_bit_comparator_4_a_b_2, n4_bit_comparator_4_a_b_3;

  _4_bit_Comparator u_4_bit_comparator_1 (
    .A(A[3:0]), .B(B[3:0]), .in_2(1'b0), .in_3(1'b0), .in_4(1'b1), .A_B(n4_bit_comparator_1_a_b),
    .A_B_2(n4_bit_comparator_1_a_b_2), .A_B_3(n4_bit_comparator_1_a_b_3));
  _4_bit_Comparator u_4_bit_comparator_2 (
    .A(A[7:4]), .B(B[7:4]), .in_2(n4_bit_comparator_1_a_b), .in_3(n4_bit_comparator_1_a_b_2),
    .in_4(n4_bit_comparator_1_a_b_3), .A_B(n4_bit_comparator_2_a_b), .A_B_2(n4_bit_comparator_2_a_b_2),
    .A_B_3(n4_bit_comparator_2_a_b_3));
  _4_bit_Comparator u_4_bit_comparator_3 (
    .A(A[11:8]), .B(B[11:8]), .in_2(n4_bit_comparator_2_a_b), .in_3(n4_bit_comparator_2_a_b_2),
    .in_4(n4_bit_comparator_2_a_b_3), .A_B(n4_bit_comparator_3_a_b), .A_B_2(n4_bit_comparator_3_a_b_2),
    .A_B_3(n4_bit_comparator_3_a_b_3));
  _4_bit_Comparator u_4_bit_comparator_4 (
    .A(A[15:12]), .B(B[15:12]), .in_2(n4_bit_comparator_3_a_b), .in_3(n4_bit_comparator_3_a_b_2),
    .in_4(n4_bit_comparator_3_a_b_3), .A_B(n4_bit_comparator_4_a_b), .A_B_2(n4_bit_comparator_4_a_b_2),
    .A_B_3(n4_bit_comparator_4_a_b_3));
  _2_bit_Comparator u_2_bit_comparator_1 (
    .A(A[17:16]), .B(B[17:16]), .in_3(n4_bit_comparator_4_a_b), .in_4(n4_bit_comparator_4_a_b_2),
    .in_5(n4_bit_comparator_4_a_b_3), .A_B(A_B), .A_B_2(A_B_2), .A_B_3(A_B_3));
endmodule

module Full_Adder (
  input  A,
  input  B,
  input  Ci,
  output CO,
  output S
);

  wire and_1_out, and_2_out, and_3_out, xor_1_out;

  and and_1 (and_1_out, A, B);
  and and_2 (and_2_out, A, Ci);
  and and_3 (and_3_out, B, Ci);
  xor xor_1 (xor_1_out, A, B);
  or or_1 (CO, and_1_out, and_2_out, and_3_out);
  xor xor_2 (S, xor_1_out, Ci);
endmodule

module _11_bit_Adder (
  input  [10:0] SRC2,
  input  [10:0] SRC1,
  input  CarryIn,
  output [10:0] Output
);

  wire full_adder_1_co, full_adder_3_co, full_adder_4_co, full_adder_5_co, full_adder_6_co, full_adder_7_co,
       full_adder_8_co, full_adder_9_co, full_adder_10_co, full_adder_11_co;

  // Probe on SRC2
  // Probe on Output
  Full_Adder full_adder_1 (.A(SRC1[9]), .B(SRC2[9]), .Ci(full_adder_3_co), .CO(full_adder_1_co), .S(Output[9]));
  Full_Adder full_adder_2 (.A(SRC1[10]), .B(SRC2[10]), .Ci(full_adder_1_co), .S(Output[10]));  // open: CO
  Full_Adder full_adder_3 (.A(SRC1[8]), .B(SRC2[8]), .Ci(full_adder_4_co), .CO(full_adder_3_co), .S(Output[8]));
  Full_Adder full_adder_4 (.A(SRC1[7]), .B(SRC2[7]), .Ci(full_adder_6_co), .CO(full_adder_4_co), .S(Output[7]));
  Full_Adder full_adder_5 (.A(SRC1[5]), .B(SRC2[5]), .Ci(full_adder_7_co), .CO(full_adder_5_co), .S(Output[5]));
  Full_Adder full_adder_6 (.A(SRC1[6]), .B(SRC2[6]), .Ci(full_adder_5_co), .CO(full_adder_6_co), .S(Output[6]));
  Full_Adder full_adder_7 (.A(SRC1[4]), .B(SRC2[4]), .Ci(full_adder_8_co), .CO(full_adder_7_co), .S(Output[4]));
  Full_Adder full_adder_8 (.A(SRC1[3]), .B(SRC2[3]), .Ci(full_adder_10_co), .CO(full_adder_8_co), .S(Output[3]));
  Full_Adder full_adder_9 (.A(SRC1[1]), .B(SRC2[1]), .Ci(full_adder_11_co), .CO(full_adder_9_co), .S(Output[1]));
  Full_Adder full_adder_10 (.A(SRC1[2]), .B(SRC2[2]), .Ci(full_adder_9_co), .CO(full_adder_10_co), .S(Output[2]));
  Full_Adder full_adder_11 (.A(SRC1[0]), .B(SRC2[0]), .Ci(CarryIn), .CO(full_adder_11_co), .S(Output[0]));
  // Probe on SRC1
endmodule

module _18_bit_adder (
  input  [17:0] SRC2,
  input  [17:0] SRC1,
  input  CarryIn,
  output [17:0] Output
);

  wire full_adder_2_co, full_adder_3_co, full_adder_4_co, full_adder_5_co, full_adder_6_co, full_adder_7_co,
       full_adder_8_co, full_adder_9_co, full_adder_10_co, full_adder_11_co, full_adder_12_co,
       full_adder_13_co, full_adder_14_co, full_adder_15_co, full_adder_16_co, full_adder_17_co,
       full_adder_18_co;

  // Probe on SRC2
  // Probe on Output
  Full_Adder full_adder_1 (.A(SRC1[17]), .B(SRC2[17]), .Ci(full_adder_2_co), .S(Output[17]));  // open: CO
  Full_Adder full_adder_2 (.A(SRC1[16]), .B(SRC2[16]), .Ci(full_adder_3_co), .CO(full_adder_2_co), .S(Output[16]));
  Full_Adder full_adder_3 (.A(SRC1[15]), .B(SRC2[15]), .Ci(full_adder_5_co), .CO(full_adder_3_co), .S(Output[15]));
  Full_Adder full_adder_4 (.A(SRC1[13]), .B(SRC2[13]), .Ci(full_adder_6_co), .CO(full_adder_4_co), .S(Output[13]));
  Full_Adder full_adder_5 (.A(SRC1[14]), .B(SRC2[14]), .Ci(full_adder_4_co), .CO(full_adder_5_co), .S(Output[14]));
  Full_Adder full_adder_6 (.A(SRC1[12]), .B(SRC2[12]), .Ci(full_adder_7_co), .CO(full_adder_6_co), .S(Output[12]));
  Full_Adder full_adder_7 (.A(SRC1[11]), .B(SRC2[11]), .Ci(full_adder_9_co), .CO(full_adder_7_co), .S(Output[11]));
  Full_Adder full_adder_8 (.A(SRC1[9]), .B(SRC2[9]), .Ci(full_adder_11_co), .CO(full_adder_8_co), .S(Output[9]));
  Full_Adder full_adder_9 (.A(SRC1[10]), .B(SRC2[10]), .Ci(full_adder_8_co), .CO(full_adder_9_co), .S(Output[10]));
  Full_Adder full_adder_10 (.A(SRC1[7]), .B(SRC2[7]), .Ci(full_adder_12_co), .CO(full_adder_10_co), .S(Output[7]));
  Full_Adder full_adder_11 (.A(SRC1[8]), .B(SRC2[8]), .Ci(full_adder_10_co), .CO(full_adder_11_co), .S(Output[8]));
  Full_Adder full_adder_12 (.A(SRC1[6]), .B(SRC2[6]), .Ci(full_adder_13_co), .CO(full_adder_12_co), .S(Output[6]));
  Full_Adder full_adder_13 (.A(SRC1[5]), .B(SRC2[5]), .Ci(full_adder_15_co), .CO(full_adder_13_co), .S(Output[5]));
  Full_Adder full_adder_14 (.A(SRC1[3]), .B(SRC2[3]), .Ci(full_adder_16_co), .CO(full_adder_14_co), .S(Output[3]));
  Full_Adder full_adder_15 (.A(SRC1[4]), .B(SRC2[4]), .Ci(full_adder_14_co), .CO(full_adder_15_co), .S(Output[4]));
  Full_Adder full_adder_16 (.A(SRC1[2]), .B(SRC2[2]), .Ci(full_adder_17_co), .CO(full_adder_16_co), .S(Output[2]));
  Full_Adder full_adder_17 (.A(SRC1[1]), .B(SRC2[1]), .Ci(full_adder_18_co), .CO(full_adder_17_co), .S(Output[1]));
  Full_Adder full_adder_18 (.A(SRC1[0]), .B(SRC2[0]), .Ci(CarryIn), .CO(full_adder_18_co), .S(Output[0]));
  // Probe on SRC1
endmodule

module D_Latch (
  input  D,
  input  Clock,
  output out_3
);

  wire and_1_out, and_2_out, nor_1_out;

  and and_1 (and_1_out, D, Clock);
  and and_2 (and_2_out, Clock, ~D);  // AND_Gate
  nor nor_1 (nor_1_out, and_1_out, out_3);
  nor nor_2 (out_3, nor_1_out, and_2_out);
endmodule

module Flip_Flop (
  input  D,
  input  Clock,
  output Q
);

  wire d_latch_1_out_3, not_1_out;

  D_Latch d_latch_1 (.D(D), .Clock(not_1_out), .out_3(d_latch_1_out_3));
  not not_1 (not_1_out, Clock);
  D_Latch d_latch_2 (.D(d_latch_1_out_3), .Clock(Clock), .out_3(Q));
endmodule

module _1_bit_Register (
  input  Input,
  input  Enable,
  input  Clear,
  input  Clock,
  output out_5
);

  wire multiplexer_1_out, multiplexer_2_out;

  Multiplexer #(.enable("false")) multiplexer_1 (.in0(out_5), .in1(Input), .out(multiplexer_1_out), .sel(Enable));
  Multiplexer #(.enable("false")) multiplexer_2 (
    .in0(multiplexer_1_out), .in1(1'b0), .out(multiplexer_2_out), .sel(Clear));
  Flip_Flop ff_1 (.D(multiplexer_2_out), .Clock(Clock), .Q(out_5));
endmodule

module _4_bit_Register (
  input  [3:0] Input,
  input  Enable,
  input  Clear,
  input  Clock,
  output [3:0] Output
);

  wire [3:0] multiplexer_1_out, multiplexer_2_out;

  Multiplexer #(.width(4), .enable("false")) multiplexer_1 (
    .in0(Output), .in1(Input), .out(multiplexer_1_out), .sel(Enable));
  Multiplexer #(.width(4), .enable("false")) multiplexer_2 (
    .in0(multiplexer_1_out), .in1(4'b0000), .out(multiplexer_2_out), .sel(Clear));
  Flip_Flop ff_1 (.D(multiplexer_2_out[3]), .Clock(Clock), .Q(Output[3]));
  Flip_Flop ff_2 (.D(multiplexer_2_out[1]), .Clock(Clock), .Q(Output[1]));
  Flip_Flop ff_3 (.D(multiplexer_2_out[2]), .Clock(Clock), .Q(Output[2]));
  Flip_Flop ff_4 (.D(multiplexer_2_out[0]), .Clock(Clock), .Q(Output[0]));
endmodule

module _11_bit_Register (
  input  [10:0] Input,
  input  Enable,
  input  Clear,
  input  Clock,
  output [10:0] Output
);

  wire [10:0] multiplexer_1_out, multiplexer_2_out;

  Multiplexer #(.width(11), .enable("false")) multiplexer_1 (
    .in0(Output), .in1(Input), .out(multiplexer_1_out), .sel(Enable));
  Multiplexer #(.width(11), .enable("false")) multiplexer_2 (
    .in0(multiplexer_1_out), .in1({11{1'b0}}), .out(multiplexer_2_out), .sel(Clear));
  Flip_Flop ff_1 (.D(multiplexer_2_out[10]), .Clock(Clock), .Q(Output[10]));
  Flip_Flop ff_2 (.D(multiplexer_2_out[9]), .Clock(Clock), .Q(Output[9]));
  Flip_Flop ff_3 (.D(multiplexer_2_out[7]), .Clock(Clock), .Q(Output[7]));
  Flip_Flop ff_4 (.D(multiplexer_2_out[8]), .Clock(Clock), .Q(Output[8]));
  Flip_Flop ff_5 (.D(multiplexer_2_out[6]), .Clock(Clock), .Q(Output[6]));
  Flip_Flop ff_6 (.D(multiplexer_2_out[5]), .Clock(Clock), .Q(Output[5]));
  Flip_Flop ff_7 (.D(multiplexer_2_out[4]), .Clock(Clock), .Q(Output[4]));
  Flip_Flop ff_8 (.D(multiplexer_2_out[3]), .Clock(Clock), .Q(Output[3]));
  Flip_Flop ff_9 (.D(multiplexer_2_out[1]), .Clock(Clock), .Q(Output[1]));
  Flip_Flop ff_10 (.D(multiplexer_2_out[2]), .Clock(Clock), .Q(Output[2]));
  Flip_Flop ff_11 (.D(multiplexer_2_out[0]), .Clock(Clock), .Q(Output[0]));
endmodule

module _18_bit_Register (
  input  [17:0] Input,
  input  Enable,
  input  Clear,
  input  Clock,
  output [17:0] Output
);

  wire [17:0] multiplexer_1_out, multiplexer_2_out;

  Multiplexer #(.width(18), .enable("false")) multiplexer_1 (
    .in0(Output), .in1(Input), .out(multiplexer_1_out), .sel(Enable));
  Multiplexer #(.width(18), .enable("false")) multiplexer_2 (
    .in0(multiplexer_1_out), .in1({18{1'b0}}), .out(multiplexer_2_out), .sel(Clear));
  Flip_Flop ff_1 (.D(multiplexer_2_out[17]), .Clock(Clock), .Q(Output[17]));
  Flip_Flop ff_2 (.D(multiplexer_2_out[16]), .Clock(Clock), .Q(Output[16]));
  Flip_Flop ff_3 (.D(multiplexer_2_out[15]), .Clock(Clock), .Q(Output[15]));
  Flip_Flop ff_4 (.D(multiplexer_2_out[14]), .Clock(Clock), .Q(Output[14]));
  Flip_Flop ff_5 (.D(multiplexer_2_out[13]), .Clock(Clock), .Q(Output[13]));
  Flip_Flop ff_6 (.D(multiplexer_2_out[12]), .Clock(Clock), .Q(Output[12]));
  Flip_Flop ff_7 (.D(multiplexer_2_out[10]), .Clock(Clock), .Q(Output[10]));
  Flip_Flop ff_8 (.D(multiplexer_2_out[11]), .Clock(Clock), .Q(Output[11]));
  Flip_Flop ff_9 (.D(multiplexer_2_out[9]), .Clock(Clock), .Q(Output[9]));
  Flip_Flop ff_10 (.D(multiplexer_2_out[8]), .Clock(Clock), .Q(Output[8]));
  Flip_Flop ff_11 (.D(multiplexer_2_out[7]), .Clock(Clock), .Q(Output[7]));
  Flip_Flop ff_12 (.D(multiplexer_2_out[6]), .Clock(Clock), .Q(Output[6]));
  Flip_Flop ff_13 (.D(multiplexer_2_out[4]), .Clock(Clock), .Q(Output[4]));
  Flip_Flop ff_14 (.D(multiplexer_2_out[5]), .Clock(Clock), .Q(Output[5]));
  Flip_Flop ff_15 (.D(multiplexer_2_out[3]), .Clock(Clock), .Q(Output[3]));
  Flip_Flop ff_16 (.D(multiplexer_2_out[2]), .Clock(Clock), .Q(Output[2]));
  Flip_Flop ff_17 (.D(multiplexer_2_out[1]), .Clock(Clock), .Q(Output[1]));
  Flip_Flop ff_18 (.D(multiplexer_2_out[0]), .Clock(Clock), .Q(Output[0]));
endmodule
